# Fritzing sketch larabot_layout (saved by Fritzing 0.9.2b)
breadboards: 1

parts:
  Arduino_Uno = Arduino Uno (Rev3)
  Tilt = Basic Servo
  Pan = Basic Servo

nets:
  N1: Arduino_Uno.D9_PWM, Tilt.pulse
  N2: Arduino_Uno.D10_PWM/SS, Pan.pulse
  VCC: Arduino_Uno.5V, Tilt.vcc, Pan.vcc
  GND: Arduino_Uno.GND, Tilt.gnd, Pan.gnd
